// Digital circuit ALU.dig as structural Verilog
module ALU (
  input  Ctrl_In,
  input  Ctrl_Out,
  input  Clk,
  input  [31:0] Data_In,
  input  Sel_A,
  input  Sel_B,
  input  Sel_SUM,
  input  Sel_AND,
  input  Sel_OR,
  input  Sel_XOR,
  input  Sel_NOT,
  input  Sel_GT,
  input  Sel_GTE,
  input  Sel_LT,
  input  Sel_LTE,
  output [31:0] Data_Out
);

  wire and_1_out, and_2_out, and_3_out, and_4_out, and_5_out, and_6_out, and_7_out, and_8_out, and_9_out;
  wire [31:0] add_1_s, and_14_out, not_1_out, or_1_out, register_1_q, register_2_q, xor_1_out;

  and and_1 (and_1_out, Ctrl_Out, Sel_A);
  and and_2 (and_2_out, Sel_A, Ctrl_In);
  and and_3 (and_3_out, Ctrl_Out, Sel_B);
  and and_4 (and_4_out, Sel_B, Ctrl_In);
  and and_5 (and_5_out, Ctrl_Out, Sel_SUM);
  and and_6 (and_6_out, Ctrl_Out, Sel_AND);
  and and_7 (and_7_out, Ctrl_Out, Sel_OR);
  and and_8 (and_8_out, Ctrl_Out, Sel_XOR);
  and and_9 (and_9_out, Ctrl_Out, Sel_NOT);
  // And and_10 has open pins: In_1=Ctrl_Out, In_2=Sel_GT, out=open
  // And and_11 has open pins: In_1=Ctrl_Out, In_2=Sel_GTE, out=open
  // And and_12 has open pins: In_1=Ctrl_Out, In_2=Sel_LT, out=open
  // And and_13 has open pins: In_1=Ctrl_Out, In_2=Sel_LTE, out=open
  Register #(.Bits(32)) register_1 (.D(Data_In), .C(Clk), .en(and_2_out), .Q(register_1_q));
  Register #(.Bits(32)) register_2 (.D(Data_In), .C(Clk), .en(and_4_out), .Q(register_2_q));
  assign Data_Out = and_1_out ? register_1_q : 32'bz;  // Driver driver_1
  assign Data_Out = and_3_out ? register_2_q : 32'bz;  // Driver driver_2
  Add #(.Bits(32)) add_1 (.a(register_1_q), .b(register_2_q), .c_i(1'b0), .s(add_1_s));  // open: c_o
  assign and_14_out = register_1_q & register_2_q;  // And and_14, 32 bits wide
  assign or_1_out = register_1_q | register_2_q;  // Or or_1, 32 bits wide
  assign xor_1_out = register_1_q ^ register_2_q;  // XOr xor_1, 32 bits wide
  assign not_1_out = ~register_1_q;  // Not not_1, 32 bits wide
  assign Data_Out = and_5_out ? add_1_s : 32'bz;  // Driver driver_3
  assign Data_Out = and_6_out ? and_14_out : 32'bz;  // Driver driver_4
  assign Data_Out = and_7_out ? or_1_out : 32'bz;  // Driver driver_5
  assign Data_Out = and_8_out ? xor_1_out : 32'bz;  // Driver driver_6
  assign Data_Out = and_9_out ? not_1_out : 32'bz;  // Driver driver_7
endmodule
