// Digital circuit MMP-1.dig as structural Verilog
module MMP_1 (
  input  _4Hz,
  input  _100Hz,
  input  clk
);

  wire Addr_Dest, Addr_Src, Addr_Step, alu_1_data_ready, and_1_out, and_2_out, and_3_out, and_4_out,
       and_5_out, and_6_out, and_7_out, and_8_out, and_9_out, and_10_out, and_11_out, and_12_out, and_13_out,
       and_14_out, and_15_out, and_16_out, and_17_out, and_18_out, and_19_out, and_20_out, buttonled_1_p1,
       buttonled_1_p2, buttonled_2_p1, buttonled_2_p2, buttonled_3_p1, buttonled_3_p2, buttonled_4_p1,
       buttonled_4_p2, Clk_t, comparator_1_eq, comparator_2_eq, comparator_3_eq, comparator_3_gt,
       comparator_3_lt, comparator_4_lt, comparator_5_eq, comparator_6_eq, comparator_7_eq, comparator_8_eq,
       counter_1_ovf, demultiplexer_1_out_0, demultiplexer_1_out_1, demultiplexer_1_out_2,
       demultiplexer_1_out_3, nClk, not_1_out, not_2_out, not_3_out, not_4_out, nRst, or_1_out, or_2_out,
       Out_Dev, Res_out, rs_ff_as_2_q, rs_ff_as_3_q, rs_ff_as_4_nq, rs_ff_as_4_q, rs_ff_as_5_q, Rst,
       Step_2_out, Step_Inc, undriven, undriven_2, undriven_3, undriven_4, undriven_5, undriven_6,
       undriven_7, undriven_8, undriven_9, undriven_10, undriven_11, undriven_12, undriven_13, undriven_14,
       undriven_15, undriven_16, undriven_17, undriven_18, undriven_19, undriven_20, undriven_21,
       undriven_22, undriven_23, undriven_24, undriven_25, undriven_26, undriven_27, undriven_28,
       undriven_29, undriven_30, undriven_31, undriven_32, undriven_33, undriven_34, undriven_35,
       undriven_36, undriven_37, undriven_38, undriven_39, undriven_40, undriven_41, undriven_42,
       undriven_43, undriven_44, undriven_45, undriven_46, undriven_47, undriven_48, undriven_49,
       undriven_50, undriven_51, undriven_52, undriven_53, undriven_54, undriven_55, undriven_56,
       undriven_57, undriven_58, undriven_59, undriven_60, undriven_61, undriven_62, undriven_63,
       undriven_64, undriven_65, undriven_66, undriven_67, undriven_68, undriven_69, undriven_70,
       undriven_71, undriven_72, undriven_73, undriven_74, undriven_75, undriven_76, undriven_77,
       undriven_78, undriven_79, undriven_80, undriven_81, undriven_82, undriven_83, undriven_84,
       undriven_85, undriven_86, undriven_87, undriven_88, undriven_89, undriven_90, undriven_91,
       undriven_92, undriven_93, undriven_94, undriven_95, undriven_96, undriven_97, undriven_98,
       undriven_99, undriven_100, undriven_101, undriven_102, undriven_103, undriven_104, undriven_105,
       undriven_106, undriven_107, undriven_108, undriven_109, undriven_110, undriven_111, undriven_112,
       undriven_113, undriven_114, undriven_115, undriven_116, undriven_117, undriven_118, undriven_119,
       undriven_120, undriven_121, undriven_122, undriven_123, undriven_124, undriven_125, undriven_126,
       undriven_127, undriven_128, undriven_129, undriven_130, undriven_131, undriven_132, undriven_133,
       undriven_134, undriven_135, undriven_136, undriven_137, undriven_138, undriven_139, undriven_140,
       undriven_141, undriven_142, undriven_143, undriven_144, undriven_145, undriven_146, undriven_147,
       undriven_148, undriven_149, undriven_150, undriven_151, undriven_152, undriven_153, undriven_154,
       undriven_155, undriven_156, undriven_157, undriven_158, undriven_159, undriven_160, undriven_161,
       undriven_162, undriven_163, undriven_164, undriven_165, undriven_166, undriven_167, undriven_168,
       undriven_169, undriven_170, undriven_171, undriven_172, undriven_173, undriven_174, undriven_175,
       undriven_176, undriven_177, undriven_178, undriven_179, undriven_180, undriven_181, undriven_182,
       undriven_183, undriven_184, undriven_185, undriven_186, undriven_187, undriven_188, undriven_189,
       undriven_190, undriven_191, undriven_192, undriven_193, undriven_194, undriven_195, undriven_196,
       undriven_197, undriven_198, undriven_199, undriven_200, undriven_201, undriven_202, undriven_203,
       undriven_204, undriven_205, undriven_206, undriven_207, undriven_208, undriven_209, undriven_210,
       undriven_211, undriven_212, undriven_213, undriven_214, undriven_215, undriven_216, undriven_217,
       undriven_218, undriven_219, undriven_220, undriven_221, undriven_222, undriven_223, undriven_224,
       undriven_225, undriven_226, undriven_227, undriven_228, undriven_229, undriven_230, undriven_231,
       undriven_232, undriven_233, undriven_234, undriven_235, undriven_236, undriven_237, undriven_238,
       undriven_239, undriven_240, undriven_241, undriven_242, undriven_243, undriven_244, undriven_245,
       undriven_246, undriven_247, undriven_248, undriven_249, undriven_250, undriven_251, undriven_252,
       undriven_253, undriven_254, undriven_255, undriven_256;
  wire [1:0] clockselect_1_num, counter_1_out, counter_2_out, multiplexer_13_out;
  wire [4:0] MatrixXIndex_q;
  wire [13:0] Addr_Match_out;
  wire [15:0] Addr, Dest, multiplexer_2_out, multiplexer_3_out, multiplexer_13_out_3, PrgmStep, Src;
  wire [15:2] multiplexer_13_out_2;
  wire [31:0] alu_1_data_out, DispA, DispB, MatrixCValues_q, multiplexer_1_out, multiplexer_5_out,
       multiplexer_6_out, multiplexer_7_out, multiplexer_8_out, multiplexer_9_out, multiplexer_10_out,
       multiplexer_11_out, multiplexer_12_out, ramdualport_1_d, rom_1_d, Temp_q;

  Button Res (.out(Res_out));
  RS_FF_AS rs_ff_as_1 (.S(Res_out), .R(counter_1_ovf), .Q(Rst), .nQ(nRst));
  Register #(.Bits(32)) Temp (
    .D({multiplexer_13_out_3, multiplexer_13_out_2, multiplexer_13_out}), .C(Clk_t), .en(Addr_Src), .Q(Temp_q));
  Register #(.Bits(16)) u_Src (.D(multiplexer_13_out_3), .C(Clk_t), .en(Addr_Step), .Q(Src));
  Register #(.Bits(16)) u_Dest (.D({multiplexer_13_out_2, multiplexer_13_out}), .C(Clk_t), .en(Addr_Step), .Q(Dest));
  Comparator #(.Bits(16)) comparator_1 (.a(Dest), .b({16{1'b1}}), .eq(comparator_1_eq));  // open: gt, lt
  and and_1 (and_1_out, Addr_Dest, comparator_1_eq);
  CounterPreset #(.Bits(16)) Step (
    .en(and_2_out), .C(Clk_t), .dir(1'b0), .in({multiplexer_13_out_2, multiplexer_13_out}), .ld(and_1_out),
    .clr(Rst), .out(PrgmStep));  // open: ovf
  Multiplexer #(.Bits(32)) multiplexer_1 (.sel(Addr_Dest), .in_0({32{1'b0}}), .in_1(Temp_q), .out(multiplexer_1_out));
  and and_2 (and_2_out, Step_Inc, not_1_out);
  Counter #(.Bits(2)) counter_1 (.en(Rst), .C(nClk), .clr(nRst), .out(counter_1_out), .ovf(counter_1_ovf));
  Multiplexer #(.Bits(16)) multiplexer_2 (.sel(Addr_Src), .in_0({16{1'b0}}), .in_1(Src), .out(multiplexer_2_out));
  Multiplexer #(.Bits(16)) multiplexer_3 (
    .sel(Addr_Dest), .in_0(multiplexer_2_out), .in_1(Dest), .out(multiplexer_3_out));
  not not_1 (not_1_out, comparator_1_eq);
  Multiplexer #(.Bits(16)) multiplexer_4 (.sel(Addr_Step), .in_0(multiplexer_3_out), .in_1(PrgmStep), .out(Addr));
  not not_2 (not_2_out, Addr_Step);
  Button Step_2 (.out(Step_2_out));
  not not_3 (not_3_out, Step_2_out);
  RS_FF_AS rs_ff_as_2 (.S(not_3_out), .R(or_2_out), .Q(rs_ff_as_2_q));  // open: nQ
  RS_FF_AS rs_ff_as_3 (.S(not_2_out), .R(rs_ff_as_4_nq), .Q(rs_ff_as_3_q));  // open: nQ
  Comparator #(.Bits(16)) comparator_2 (.a(Addr), .b(16'hfff0), .eq(comparator_2_eq));  // open: gt, lt
  Comparator #(.Bits(16)) comparator_3 (
    .a(Addr), .b(16'h4000), .gt(comparator_3_gt), .eq(comparator_3_eq), .lt(comparator_3_lt));
  Comparator #(.Bits(16)) comparator_4 (.a(Addr), .b(16'h8000), .lt(comparator_4_lt));  // open: gt, eq
  // Probe Source on Src
  // Probe Destination on Dest
  and and_3 (and_3_out, Step_2_out, rs_ff_as_2_q);
  and and_4 (and_4_out, Addr_Step, rs_ff_as_3_q);
  RS_FF_AS rs_ff_as_4 (.S(and_3_out), .R(or_2_out), .Q(rs_ff_as_4_q), .nQ(rs_ff_as_4_nq));
  RS_FF_AS rs_ff_as_5 (.S(and_4_out), .R(rs_ff_as_4_nq), .Q(rs_ff_as_5_q));  // open: nQ
  and and_5 (and_5_out, Addr_Dest, comparator_2_eq);
  and and_6 (and_6_out, comparator_2_eq, Out_Dev);
  or or_1 (or_1_out, comparator_3_gt, comparator_3_eq);
  and and_7 (and_7_out, or_1_out, comparator_4_lt);
  or or_2 (or_2_out, rs_ff_as_5_q, not_4_out);
  // Probe Program Step on PrgmStep
  // Probe Address on Addr
  // Probe Bus on {multiplexer_13_out_3, multiplexer_13_out_2, multiplexer_13_out}
  // ButtonLED buttonled_1: pin names not known; wires that end beside it: buttonled_1_p1, buttonled_1_p2
  // ButtonLED buttonled_2: pin names not known; wires that end beside it: buttonled_2_p1, buttonled_2_p2
  // ButtonLED buttonled_3: pin names not known; wires that end beside it: buttonled_3_p1, buttonled_3_p2
  // ButtonLED buttonled_4: pin names not known; wires that end beside it: buttonled_4_p1, buttonled_4_p2
  and and_8 (and_8_out, clk, rs_ff_as_4_q);
  not not_4 (not_4_out, buttonled_2_p2);
  and and_9 (and_9_out, comparator_3_lt, Out_Dev);
  and and_10 (and_10_out, comparator_3_lt, Addr_Dest);
  and and_11 (and_11_out, Addr_Dest, and_7_out);
  and and_12 (and_12_out, and_7_out, Out_Dev);
  ClockSelect clockselect_1 (
    .ManA(buttonled_1_p1), .ManB(buttonled_2_p1), .ManC(buttonled_3_p1), .ManD(buttonled_4_p1),
    .ClkA(Step_2_out), .ClkB(and_8_out), .ClkC(_4Hz), .ClkD(_100Hz), .AutoA(demultiplexer_1_out_0),
    .AutoB(demultiplexer_1_out_1), .AutoC(demultiplexer_1_out_2), .AutoD(demultiplexer_1_out_3),
    .DispA(buttonled_1_p2), .DispB(buttonled_2_p2), .DispC(buttonled_3_p2), .DispD(buttonled_4_p2),
    .Clk(Clk_t), .nClk(nClk), .Num(clockselect_1_num));
  Demultiplexer #(.Selector_Bits(2)) demultiplexer_1 (
    .sel(multiplexer_13_out), .in(and_5_out), .out_0(demultiplexer_1_out_0), .out_1(demultiplexer_1_out_1),
    .out_2(demultiplexer_1_out_2), .out_3(demultiplexer_1_out_3));
  ROM #(.bigEndian("true"), .AddrBits(14), .Bits(32)) rom_1 (.A(Addr[13:0]), .sel(1'b1), .D(rom_1_d));
  LED ErrROMWrite (.in(and_10_out));
  RAMDualPort #(.AddrBits(14), .Bits(32)) ramdualport_1 (
    .A(Addr[13:0]), .Din({multiplexer_13_out_3, multiplexer_13_out_2, multiplexer_13_out}), .str(and_11_out),
    .C(Clk_t), .ld(1'b1), .D(ramdualport_1_d));
  // Probe on clockselect_1_num
  Multiplexer #(.Bits(32)) multiplexer_5 (
    .sel(and_6_out), .in_0(multiplexer_1_out), .in_1({{30{1'b0}}, clockselect_1_num}), .out(multiplexer_5_out));
  Multiplexer #(.Bits(32)) multiplexer_6 (
    .sel(and_9_out), .in_0(multiplexer_5_out), .in_1(rom_1_d), .out(multiplexer_6_out));
  Multiplexer #(.Bits(32)) multiplexer_7 (
    .sel(and_12_out), .in_0(multiplexer_6_out), .in_1(ramdualport_1_d), .out(multiplexer_7_out));
  Counter #(.Bits(2)) counter_2 (.en(1'b1), .C(nClk), .clr(Rst), .out(counter_2_out));  // open: ovf
  Decoder #(.Selector_Bits(2)) decoder_1 (
    .sel(counter_2_out), .out_0(Addr_Step), .out_1(Addr_Src), .out_2(Addr_Dest), .out_3(Step_Inc));
  Comparator #(.Bits(16)) comparator_5 (.a(Addr), .b(16'hf100), .eq(comparator_5_eq));  // open: gt, lt
  Comparator #(.Bits(16)) comparator_6 (.a(Addr), .b(16'hf101), .eq(comparator_6_eq));  // open: gt, lt
  Comparator #(.Bits(16)) comparator_7 (.a(Addr), .b(16'hf200), .eq(comparator_7_eq));  // open: gt, lt
  Comparator #(.Bits(16)) comparator_8 (.a(Addr), .b(16'hf201), .eq(comparator_8_eq));  // open: gt, lt
  LookUpTable #(.Bits(14)) Addr_Match (
    .in0(Addr[0]), .in1(Addr[1]), .in2(Addr[2]), .in3(Addr[3]), .in4(Addr[4]), .in5(Addr[5]), .in6(Addr[6]),
    .in7(Addr[7]), .in8(Addr[8]), .in9(Addr[9]), .in10(Addr[10]), .in11(Addr[11]), .in12(Addr[12]),
    .in13(Addr[13]), .in14(Addr[14]), .in15(Addr[15]), .out(Addr_Match_out));
  and and_13 (and_13_out, Addr_Dest, comparator_5_eq);
  and and_14 (and_14_out, comparator_5_eq, Out_Dev);
  and and_15 (and_15_out, Addr_Dest, comparator_6_eq);
  and and_16 (and_16_out, comparator_6_eq, Out_Dev);
  and and_17 (and_17_out, Addr_Dest, comparator_7_eq);
  and and_18 (and_18_out, comparator_7_eq, Out_Dev);
  and and_19 (and_19_out, Addr_Dest, comparator_8_eq);
  and and_20 (and_20_out, comparator_8_eq, Out_Dev);
  or or_3 (Out_Dev, Addr_Src, Addr_Step);
  Register #(.Bits(32)) u_DispA (
    .D({multiplexer_13_out_3, multiplexer_13_out_2, multiplexer_13_out}), .C(Clk_t), .en(and_13_out),
    .Q(DispA));
  Register #(.Bits(32)) u_DispB (
    .D({multiplexer_13_out_3, multiplexer_13_out_2, multiplexer_13_out}), .C(Clk_t), .en(and_15_out),
    .Q(DispB));
  Register #(.Bits(5)) MatrixXIndex (
    .D({multiplexer_13_out_2[4:2], multiplexer_13_out}), .C(Clk_t), .en(and_17_out), .Q(MatrixXIndex_q));
  Register #(.Bits(32)) MatrixCValues (
    .D({multiplexer_13_out_3, multiplexer_13_out_2, multiplexer_13_out}), .C(Clk_t), .en(and_19_out),
    .Q(MatrixCValues_q));
  ALU alu_1 (
    .Ctrl_In(Addr_Dest), .Ctrl_Out(Out_Dev), .Clk(Clk_t),
    .Data_In({multiplexer_13_out_3, multiplexer_13_out_2, multiplexer_13_out}), .Sel_A(Addr_Match_out[0]),
    .Sel_B(Addr_Match_out[1]), .Sel_SUM(Addr_Match_out[2]), .Sel_DIF(Addr_Match_out[3]),
    .Sel_LSH(Addr_Match_out[4]), .Sel_RSH(Addr_Match_out[5]), .Sel_AND(Addr_Match_out[6]),
    .Sel_OR(Addr_Match_out[7]), .Sel_XOR(Addr_Match_out[8]), .Sel_NOT(Addr_Match_out[9]),
    .Sel_GT(Addr_Match_out[10]), .Sel_GTE(Addr_Match_out[11]), .Sel_LT(Addr_Match_out[12]),
    .Sel_LTE(Addr_Match_out[13]), .Data_Out(alu_1_data_out), .Data_Ready(alu_1_data_ready));
  LED led_1 (.in(Addr_Step));
  LED led_2 (.in(Addr_Src));
  LED led_3 (.in(Addr_Dest));
  LED led_4 (.in(Step_Inc));
  LedMatrix #(.colAddrBits(5), .rowDataBits(32)) ledmatrix_1 (.rows(MatrixCValues_q), .column(MatrixXIndex_q));
  Multiplexer #(.Bits(32)) multiplexer_8 (
    .sel(and_14_out), .in_0(multiplexer_7_out), .in_1(DispA), .out(multiplexer_8_out));
  Multiplexer #(.Bits(32)) multiplexer_9 (
    .sel(and_16_out), .in_0(multiplexer_8_out), .in_1(DispB), .out(multiplexer_9_out));
  Multiplexer #(.Bits(32)) multiplexer_10 (
    .sel(and_18_out), .in_0(multiplexer_9_out), .in_1({{27{1'b0}}, MatrixXIndex_q}), .out(multiplexer_10_out));
  Multiplexer #(.Bits(32)) multiplexer_11 (
    .sel(and_20_out), .in_0(multiplexer_10_out), .in_1(MatrixCValues_q), .out(multiplexer_11_out));
  Multiplexer #(.Bits(32)) multiplexer_12 (
    .sel(alu_1_data_ready), .in_0(multiplexer_11_out), .in_1(alu_1_data_out), .out(multiplexer_12_out));
  Multiplexer #(.Bits(32)) multiplexer_13 (
    .sel(Rst), .in_0(multiplexer_12_out), .in_1({32{1'b0}}),
    .out({multiplexer_13_out_3, multiplexer_13_out_2, multiplexer_13_out}));
  Seven_Seg_Hex seven_seg_hex_1 (.d(DispA[31:28]), .dp(1'b0));
  Seven_Seg_Hex seven_seg_hex_2 (.d(DispB[31:28]), .dp(1'b0));
  Seven_Seg_Hex seven_seg_hex_3 (.d(DispA[27:24]), .dp(1'b0));
  Seven_Seg_Hex seven_seg_hex_4 (.d(DispB[27:24]), .dp(1'b0));
  Seven_Seg_Hex seven_seg_hex_5 (.d(DispA[23:20]), .dp(1'b0));
  Seven_Seg_Hex seven_seg_hex_6 (.d(DispB[23:20]), .dp(1'b0));
  Seven_Seg_Hex seven_seg_hex_7 (.d(DispA[19:16]), .dp(1'b0));
  Seven_Seg_Hex seven_seg_hex_8 (.d(DispB[19:16]), .dp(1'b0));
  Seven_Seg_Hex seven_seg_hex_9 (.d(DispA[15:12]), .dp(1'b0));
  Seven_Seg_Hex seven_seg_hex_10 (.d(DispB[15:12]), .dp(1'b0));
  LED led_5 (.in(undriven_17));
  LED led_6 (.in(undriven));
  LED led_7 (.in(undriven_18));
  LED led_8 (.in(undriven_2));
  LED led_9 (.in(undriven_19));
  LED led_10 (.in(undriven_3));
  LED led_11 (.in(undriven_20));
  LED led_12 (.in(undriven_4));
  LED led_13 (.in(undriven_21));
  LED led_14 (.in(undriven_5));
  LED led_15 (.in(undriven_22));
  LED led_16 (.in(undriven_6));
  LED led_17 (.in(undriven_23));
  LED led_18 (.in(undriven_7));
  LED led_19 (.in(undriven_24));
  LED led_20 (.in(undriven_8));
  LED led_21 (.in(undriven_25));
  LED led_22 (.in(undriven_9));
  LED led_23 (.in(undriven_26));
  LED led_24 (.in(undriven_10));
  LED led_25 (.in(undriven_27));
  LED led_26 (.in(undriven_11));
  LED led_27 (.in(undriven_28));
  LED led_28 (.in(undriven_12));
  LED led_29 (.in(undriven_29));
  LED led_30 (.in(undriven_13));
  LED led_31 (.in(undriven_30));
  LED led_32 (.in(undriven_14));
  LED led_33 (.in(undriven_31));
  LED led_34 (.in(undriven_15));
  LED led_35 (.in(undriven_32));
  LED led_36 (.in(undriven_16));
  Seven_Seg_Hex seven_seg_hex_11 (.d(DispA[11:8]), .dp(1'b0));
  Seven_Seg_Hex seven_seg_hex_12 (.d(DispB[11:8]), .dp(1'b0));
  LED led_37 (.in(undriven_49));
  LED led_38 (.in(undriven_33));
  LED led_39 (.in(undriven_50));
  LED led_40 (.in(undriven_34));
  LED led_41 (.in(undriven_51));
  LED led_42 (.in(undriven_35));
  LED led_43 (.in(undriven_52));
  LED led_44 (.in(undriven_36));
  LED led_45 (.in(undriven_53));
  LED led_46 (.in(undriven_37));
  LED led_47 (.in(undriven_54));
  LED led_48 (.in(undriven_38));
  LED led_49 (.in(undriven_55));
  LED led_50 (.in(undriven_39));
  LED led_51 (.in(undriven_56));
  LED led_52 (.in(undriven_40));
  LED led_53 (.in(undriven_57));
  LED led_54 (.in(undriven_41));
  LED led_55 (.in(undriven_58));
  LED led_56 (.in(undriven_42));
  LED led_57 (.in(undriven_59));
  LED led_58 (.in(undriven_43));
  LED led_59 (.in(undriven_60));
  LED led_60 (.in(undriven_44));
  LED led_61 (.in(undriven_61));
  LED led_62 (.in(undriven_45));
  LED led_63 (.in(undriven_62));
  LED led_64 (.in(undriven_46));
  LED led_65 (.in(undriven_63));
  LED led_66 (.in(undriven_47));
  LED led_67 (.in(undriven_64));
  LED led_68 (.in(undriven_48));
  Seven_Seg_Hex seven_seg_hex_13 (.d(DispA[7:4]), .dp(1'b0));
  Seven_Seg_Hex seven_seg_hex_14 (.d(DispB[7:4]), .dp(1'b0));
  LED led_69 (.in(undriven_81));
  LED led_70 (.in(undriven_65));
  LED led_71 (.in(undriven_82));
  LED led_72 (.in(undriven_66));
  LED led_73 (.in(undriven_83));
  LED led_74 (.in(undriven_67));
  LED led_75 (.in(undriven_84));
  LED led_76 (.in(undriven_68));
  LED led_77 (.in(undriven_85));
  LED led_78 (.in(undriven_69));
  LED led_79 (.in(undriven_86));
  LED led_80 (.in(undriven_70));
  LED led_81 (.in(undriven_87));
  LED led_82 (.in(undriven_71));
  LED led_83 (.in(undriven_88));
  LED led_84 (.in(undriven_72));
  LED led_85 (.in(undriven_89));
  LED led_86 (.in(undriven_73));
  LED led_87 (.in(undriven_90));
  LED led_88 (.in(undriven_74));
  LED led_89 (.in(undriven_91));
  LED led_90 (.in(undriven_75));
  LED led_91 (.in(undriven_92));
  LED led_92 (.in(undriven_76));
  LED led_93 (.in(undriven_93));
  LED led_94 (.in(undriven_77));
  LED led_95 (.in(undriven_94));
  LED led_96 (.in(undriven_78));
  LED led_97 (.in(undriven_95));
  LED led_98 (.in(undriven_79));
  LED led_99 (.in(undriven_96));
  LED led_100 (.in(undriven_80));
  Seven_Seg_Hex seven_seg_hex_15 (.d(DispA[3:0]), .dp(1'b0));
  Seven_Seg_Hex seven_seg_hex_16 (.d(DispB[3:0]), .dp(1'b0));
  LED led_101 (.in(undriven_113));
  LED led_102 (.in(undriven_97));
  LED led_103 (.in(undriven_114));
  LED led_104 (.in(undriven_98));
  LED led_105 (.in(undriven_115));
  LED led_106 (.in(undriven_99));
  LED led_107 (.in(undriven_116));
  LED led_108 (.in(undriven_100));
  LED led_109 (.in(undriven_117));
  LED led_110 (.in(undriven_101));
  LED led_111 (.in(undriven_118));
  LED led_112 (.in(undriven_102));
  LED led_113 (.in(undriven_119));
  LED led_114 (.in(undriven_103));
  LED led_115 (.in(undriven_120));
  LED led_116 (.in(undriven_104));
  LED led_117 (.in(undriven_121));
  LED led_118 (.in(undriven_105));
  LED led_119 (.in(undriven_122));
  LED led_120 (.in(undriven_106));
  LED led_121 (.in(undriven_123));
  LED led_122 (.in(undriven_107));
  LED led_123 (.in(undriven_124));
  LED led_124 (.in(undriven_108));
  LED led_125 (.in(undriven_125));
  LED led_126 (.in(undriven_109));
  LED led_127 (.in(undriven_126));
  LED led_128 (.in(undriven_110));
  LED led_129 (.in(undriven_127));
  LED led_130 (.in(undriven_111));
  LED led_131 (.in(undriven_128));
  LED led_132 (.in(undriven_112));
  LED led_133 (.in(undriven_145));
  LED led_134 (.in(undriven_129));
  LED led_135 (.in(undriven_146));
  LED led_136 (.in(undriven_130));
  LED led_137 (.in(undriven_147));
  LED led_138 (.in(undriven_131));
  LED led_139 (.in(undriven_148));
  LED led_140 (.in(undriven_132));
  LED led_141 (.in(undriven_149));
  LED led_142 (.in(undriven_133));
  LED led_143 (.in(undriven_150));
  LED led_144 (.in(undriven_134));
  LED led_145 (.in(undriven_151));
  LED led_146 (.in(undriven_135));
  LED led_147 (.in(undriven_152));
  LED led_148 (.in(undriven_136));
  LED led_149 (.in(undriven_153));
  LED led_150 (.in(undriven_137));
  LED led_151 (.in(undriven_154));
  LED led_152 (.in(undriven_138));
  LED led_153 (.in(undriven_155));
  LED led_154 (.in(undriven_139));
  LED led_155 (.in(undriven_156));
  LED led_156 (.in(undriven_140));
  LED led_157 (.in(undriven_157));
  LED led_158 (.in(undriven_141));
  LED led_159 (.in(undriven_158));
  LED led_160 (.in(undriven_142));
  LED led_161 (.in(undriven_159));
  LED led_162 (.in(undriven_143));
  LED led_163 (.in(undriven_160));
  LED led_164 (.in(undriven_144));
  LED led_165 (.in(undriven_177));
  LED led_166 (.in(undriven_161));
  LED led_167 (.in(undriven_178));
  LED led_168 (.in(undriven_162));
  LED led_169 (.in(undriven_179));
  LED led_170 (.in(undriven_163));
  LED led_171 (.in(undriven_180));
  LED led_172 (.in(undriven_164));
  LED led_173 (.in(undriven_181));
  LED led_174 (.in(undriven_165));
  LED led_175 (.in(undriven_182));
  LED led_176 (.in(undriven_166));
  LED led_177 (.in(undriven_183));
  LED led_178 (.in(undriven_167));
  LED led_179 (.in(undriven_184));
  LED led_180 (.in(undriven_168));
  LED led_181 (.in(undriven_185));
  LED led_182 (.in(undriven_169));
  LED led_183 (.in(undriven_186));
  LED led_184 (.in(undriven_170));
  LED led_185 (.in(undriven_187));
  LED led_186 (.in(undriven_171));
  LED led_187 (.in(undriven_188));
  LED led_188 (.in(undriven_172));
  LED led_189 (.in(undriven_189));
  LED led_190 (.in(undriven_173));
  LED led_191 (.in(undriven_190));
  LED led_192 (.in(undriven_174));
  LED led_193 (.in(undriven_191));
  LED led_194 (.in(undriven_175));
  LED led_195 (.in(undriven_192));
  LED led_196 (.in(undriven_176));
  LED led_197 (.in(undriven_209));
  LED led_198 (.in(undriven_193));
  LED led_199 (.in(undriven_210));
  LED led_200 (.in(undriven_194));
  LED led_201 (.in(undriven_211));
  LED led_202 (.in(undriven_195));
  LED led_203 (.in(undriven_212));
  LED led_204 (.in(undriven_196));
  LED led_205 (.in(undriven_213));
  LED led_206 (.in(undriven_197));
  LED led_207 (.in(undriven_214));
  LED led_208 (.in(undriven_198));
  LED led_209 (.in(undriven_215));
  LED led_210 (.in(undriven_199));
  LED led_211 (.in(undriven_216));
  LED led_212 (.in(undriven_200));
  LED led_213 (.in(undriven_217));
  LED led_214 (.in(undriven_201));
  LED led_215 (.in(undriven_218));
  LED led_216 (.in(undriven_202));
  LED led_217 (.in(undriven_219));
  LED led_218 (.in(undriven_203));
  LED led_219 (.in(undriven_220));
  LED led_220 (.in(undriven_204));
  LED led_221 (.in(undriven_221));
  LED led_222 (.in(undriven_205));
  LED led_223 (.in(undriven_222));
  LED led_224 (.in(undriven_206));
  LED led_225 (.in(undriven_223));
  LED led_226 (.in(undriven_207));
  LED led_227 (.in(undriven_224));
  LED led_228 (.in(undriven_208));
  LED led_229 (.in(undriven_241));
  LED led_230 (.in(undriven_225));
  LED led_231 (.in(undriven_242));
  LED led_232 (.in(undriven_226));
  LED led_233 (.in(undriven_243));
  LED led_234 (.in(undriven_227));
  LED led_235 (.in(undriven_244));
  LED led_236 (.in(undriven_228));
  LED led_237 (.in(undriven_245));
  LED led_238 (.in(undriven_229));
  LED led_239 (.in(undriven_246));
  LED led_240 (.in(undriven_230));
  LED led_241 (.in(undriven_247));
  LED led_242 (.in(undriven_231));
  LED led_243 (.in(undriven_248));
  LED led_244 (.in(undriven_232));
  LED led_245 (.in(undriven_249));
  LED led_246 (.in(undriven_233));
  LED led_247 (.in(undriven_250));
  LED led_248 (.in(undriven_234));
  LED led_249 (.in(undriven_251));
  LED led_250 (.in(undriven_235));
  LED led_251 (.in(undriven_252));
  LED led_252 (.in(undriven_236));
  LED led_253 (.in(undriven_253));
  LED led_254 (.in(undriven_237));
  LED led_255 (.in(undriven_254));
  LED led_256 (.in(undriven_238));
  LED led_257 (.in(undriven_255));
  LED led_258 (.in(undriven_239));
  LED led_259 (.in(undriven_256));
  LED led_260 (.in(undriven_240));

  // Other names for the same wires on the sheet: MemAddr[13:0] = Addr[13:0]; In_Temp = Addr_Src;
  //   In_SrcDest = Addr_Step; NextInstr = Addr_Step; In_Dev = Addr_Dest; Out_Temp = Addr_Dest

  // Notes on the sheet:
  //   _4Hz: Hz: 4
  //   _100Hz: Hz: 100
  //   clk: Hz: 8
  //   0x0000-0x3FFF : ROM
  //   0x4000-0x7FFF : RAM
  //   0xF000-0xF00A : ALU A, B,
  //   SUM, AND, OR, XOR, NOT,
  //   GT, GTE, LT, LTE
  //   0xF100 : Display A
  //   0xF101 : Display B
  //   0xF200 : Matrix X index
  //   0xF201 : Matrix Column values
  //   0xFFF0 : Clock Select
  //   0xFFFF : Step
  //   Clock Generation
  //   ROM / RAM
  //   Single Clock
  //   Instruction
  //   4Hz
  //   100Hz
  //   rom_1 loads program.bin
  //   Control changes on -Clk
  //   Data changes on +Clk
  //   Hex Displays
  //   contents of Addr_Match (hex, n*v repeats v):
  //   61440*0,1,2,4,8,10,20,40,80,100,200,400,800,1000,2000
  //   Load pointers
  //   Read Source
  //   Write Destination
  //   Increment Step
endmodule
